# Fritzing sketch bunkerbox-v3 (saved by Fritzing 0.9.3b)

parts:
  Emergency_Stop_Switch = Round Pushbutton
  Power_Indicator = LED - 5mm [color="Red (633nm)" package="5 mm [THT]"]
  Power_Supply1 = NDR-240-24 Power Supply
  Industrial_Analog_Out_A = TinkerForge Industrial Analog Out Bricklet
  Industrial_Analog_Out_B = TinkerForge Industrial Analog Out Bricklet
  Industrial_Analog_Out_C = TinkerForge Industrial Analog Out Bricklet
  Step-Down_Power_Supply1 = TinkerForge Step-Down Power Supply
  RED1 = TinkerForge RED Brick  # not connected
  Master1 = TinkerForge Master Brick
  Industrial_Quad_Relay1 = TinkerForge Industrial Quad Relay Bricklet
  Master2 = TinkerForge Master Brick
  1Wire1 = Bunker 1Wire Bricklet
  Main_Heater_SSR_Controller = NuWave SSRMAN-1P [part_number=SSRMAN-1P]
  Pre_Heater_SSR_Controller = NuWave SSRMAN-1P [part_number=SSRMAN-1P]
  Main_Heater_SSR = Crydom SSR [part_number=D2425-10]
  Pre_Heater_SSR = Crydom SSR [part_number=D2425-10]
  To_Main_Heater = 4 Pin Connector
  To_Pre_Heater = 4 Pin Connector
  Transformer1 = 90-T40F3 Transformer [part_number=90-T40F3]
  To_Pump = 4 Pin Connector
  To_Temperature_Probes = 4 Pin Connector
  From_208V/240V_Main = 4 Pin Connector
  Solenoid_1 = 4 Pin Connector
  Solenoid_2 = 4 Pin Connector
  Solenoid_3 = 4 Pin Connector
  Solenoid_4 = 4 Pin Connector
  D1 = Rectifier Diode [part_number=1N4001 package="300 mil [THT]"]
  D2 = Rectifier Diode [part_number=1N4001 package="300 mil [THT]"]
  D3 = Rectifier Diode [part_number=1N4001 package="300 mil [THT]"]
  D4 = Rectifier Diode [part_number=1N4001 package="300 mil [THT]"]
  Contactor1 = SC-E2-220VAC Contactor [part_number=SC-E2-220VAC]
  Barometer1 = TinkerForge Barometer Bricklet
  Power_Distribution_Block1 = EPDB104 Power Distribution Block [part_number=EPDB104]
  Power_Distribution_Block3 = EPDB104 Power Distribution Block [part_number=EPDB104]
  Power_Distribution_Block2 = EPDB104 Power Distribution Block [part_number=EPDB104]
  Pre_Heater_Circuit_Breaker_(10_AMP) = FAZ-BX-2 Circuit Breaker [part_number=FAZ-BX-2]
  Main_Heater_Circuit_Breaker_(40_AMP) = FAZ-BX-2 Circuit Breaker [part_number=FAZ-BX-2]
  Power_Supply_and_Contactor_Breaker_(10_AMP) = FAZ-BX-2 Circuit Breaker [part_number=FAZ-BX-2]

nets:
  N1: Emergency_Stop_Switch.leg0, Power_Indicator.cathode, Contactor1.A1
  N2: Emergency_Stop_Switch.leg1, Power_Supply1.N, Transformer1.240VAC_(Orange), Power_Supply_and_Contactor_Breaker_(10_AMP).1
  N3: Power_Indicator.anode, Power_Supply1.L, Transformer1.COM_(Black), Contactor1.A2, Power_Supply_and_Contactor_Breaker_(10_AMP).3
  N4: Power_Supply1.+V#1, Step-Down_Power_Supply1.Input_6-27V
  N5: Power_Supply1.+V#2, Industrial_Quad_Relay1.0A, Industrial_Quad_Relay1.1A, Industrial_Quad_Relay1.2A, Industrial_Quad_Relay1.3A, To_Pump.1
  N6: Power_Supply1.-V#3, Step-Down_Power_Supply1.Input_GND
  N7: Power_Supply1.-V#4, Industrial_Analog_Out_C.GND, To_Pump.3, Solenoid_1.2, Solenoid_2.2, Solenoid_3.2, Solenoid_4.2, D1.anode, D2.anode, D3.anode, D4.anode
  N8: Power_Supply1.GND, Power_Distribution_Block3.pin_5
  N9: Industrial_Analog_Out_A.0-20mA_Out, Main_Heater_SSR_Controller.IN
  N10: Industrial_Analog_Out_A.GND, Main_Heater_SSR_Controller.0V#1
  N11: Industrial_Analog_Out_A.Bricklet_Connector, Master1.A
  N12: Industrial_Analog_Out_B.0-20mA_Out, Pre_Heater_SSR_Controller.IN
  N13: Industrial_Analog_Out_B.GND, Pre_Heater_SSR_Controller.0V#1
  N14: Industrial_Analog_Out_B.Bricklet_Connector, Master1.B
  N15: Industrial_Analog_Out_C.0-10V_Out, To_Pump.2
  N16: Industrial_Analog_Out_C.Bricklet_Connector, Master1.C
  N17: Master1.D, Industrial_Quad_Relay1.Bricklet_Connector
  N18: Industrial_Quad_Relay1.0B, Solenoid_1.1, D1.cathode
  N19: Industrial_Quad_Relay1.1B, Solenoid_2.1, D2.cathode
  N20: Industrial_Quad_Relay1.2B, Solenoid_3.1, D3.cathode
  N21: Industrial_Quad_Relay1.3B, Solenoid_4.1, D4.cathode
  N22: Master2.A, 1Wire1.Bricklet_Connector
  N23: Master2.B, Barometer1.Bricklet_Connector
  N24: 1Wire1.5V, To_Temperature_Probes.1
  N25: 1Wire1.1W, To_Temperature_Probes.2
  N26: 1Wire1.GND, To_Temperature_Probes.3
  N27: Main_Heater_SSR_Controller.0V#4, Pre_Heater_SSR_Controller.0V#4, Transformer1.COM_(Blue)
  N28: Main_Heater_SSR_Controller.24V, Pre_Heater_SSR_Controller.24V, Transformer1.24VAC_(Yellow)
  N29: Main_Heater_SSR_Controller.IN-(4), Main_Heater_SSR.4
  N30: Main_Heater_SSR_Controller.IN+(3), Main_Heater_SSR.+3
  N31: Pre_Heater_SSR_Controller.IN-(4), Pre_Heater_SSR.4
  N32: Pre_Heater_SSR_Controller.IN+(3), Pre_Heater_SSR.+3
  N33: Main_Heater_SSR.1, To_Main_Heater.2
  N34: Main_Heater_SSR.2, Main_Heater_Circuit_Breaker_(40_AMP).3
  N35: Pre_Heater_SSR.1, To_Pre_Heater.2
  N36: Pre_Heater_SSR.2, Pre_Heater_Circuit_Breaker_(10_AMP).3
  N37: To_Main_Heater.1, Main_Heater_Circuit_Breaker_(40_AMP).1
  N38: To_Main_Heater.3, Power_Distribution_Block3.pin_4
  N39: To_Pre_Heater.1, Pre_Heater_Circuit_Breaker_(10_AMP).1
  N40: From_208V/240V_Main.1, Power_Distribution_Block1.pin_1
  N41: From_208V/240V_Main.2, Power_Distribution_Block2.pin_1
  N42: From_208V/240V_Main.3, Power_Distribution_Block3.pin_1
  N43: Contactor1.1_L1, Pre_Heater_Circuit_Breaker_(10_AMP).2, Main_Heater_Circuit_Breaker_(40_AMP).2
  N44: Contactor1.3_L2, Pre_Heater_Circuit_Breaker_(10_AMP).4, Main_Heater_Circuit_Breaker_(40_AMP).4
  N45: Contactor1.2_T1, Power_Distribution_Block1.pin_5
  N46: Contactor1.4_T2, Power_Distribution_Block2.pin_5
  N47: Power_Distribution_Block1.pin_4, Power_Supply_and_Contactor_Breaker_(10_AMP).2
  N48: Power_Distribution_Block2.pin_4, Power_Supply_and_Contactor_Breaker_(10_AMP).4

notes:
  Connect if 208VAC
